// Digital circuit ALU.dig as structural Verilog
module ALU (
  input  [7:0] CMD,
  input  [7:0] DAT,
  input  CLK,
  output [7:0] Q
);

  wire _8_input_or_1_p2, _8_input_or_2_p2, comparator_1_eq, comparator_2_eq, comparator_3_eq,
       comparator_4_eq, comparator_5_eq, comparator_6_eq, comparator_7_eq, comparator_8_eq, comparator_9_eq,
       comparator_10_eq, comparator_11_eq, comparator_12_eq, comparator_13_eq, comparator_14_eq,
       comparator_15_eq, comparator_16_eq, comparator_17_eq, comparator_18_eq, comparator_19_eq,
       comparator_20_eq, comparator_22_eq, comparator_23_eq, comparator_24_eq, comparator_25_eq,
       comparator_26_eq, comparator_27_eq, comparator_28_eq, comparator_29_eq, flag_register_1_p2,
       flag_register_1_p3, flag_register_1_p4, flag_register_1_p5, flag_register_1_p12, incrementor_1_p10,
       or_1_out, register_1_p5, register_2_p5;

  Comparator #(.Bits(8)) comparator_1 (.a(CMD), .b(8'h1), .eq(comparator_1_eq));  // open: gt, lt
  Comparator #(.Bits(8)) comparator_2 (.a(CMD), .b(8'h1), .eq(comparator_2_eq));  // open: gt, lt
  Comparator #(.Bits(8)) comparator_3 (.a(CMD), .b(8'h1), .eq(comparator_3_eq));  // open: gt, lt
  Comparator #(.Bits(8)) comparator_4 (.a(CMD), .b(8'h1), .eq(comparator_4_eq));  // open: gt, lt
  Comparator #(.Bits(8)) comparator_5 (.a(CMD), .b(8'h1), .eq(comparator_5_eq));  // open: gt, lt
  Comparator #(.Bits(8)) comparator_6 (.a(CMD), .b(8'h1), .eq(comparator_6_eq));  // open: gt, lt
  or or_1 (or_1_out, comparator_5_eq, incrementor_1_p10);
  // Register register_1: pin names not known; wires that end beside it: DAT, comparator_1_eq, comparator_2_eq, CLK, register_1_p5, Q
  // Register register_2: pin names not known; wires that end beside it: DAT, comparator_3_eq, comparator_4_eq, CLK, register_2_p5, Q
  // Register register_3: pin names not known; wires that end beside it: DAT, or_1_out, comparator_6_eq, CLK, register_2_p5, Q
  Comparator #(.Bits(8)) comparator_7 (.a(CMD), .b(8'h1), .eq(comparator_7_eq));  // open: gt, lt
  Comparator #(.Bits(8)) comparator_8 (.a(CMD), .b(8'h1), .eq(comparator_8_eq));  // open: gt, lt
  Comparator #(.Bits(8)) comparator_9 (.a(CMD), .b(8'h1), .eq(comparator_9_eq));  // open: gt, lt
  Comparator #(.Bits(8)) comparator_10 (.a(CMD), .b(8'h1), .eq(comparator_10_eq));  // open: gt, lt
  Comparator #(.Bits(8)) comparator_11 (.a(CMD), .b(8'h1), .eq(comparator_11_eq));  // open: gt, lt
  Comparator #(.Bits(8)) comparator_12 (.a(CMD), .b(8'h1), .eq(comparator_12_eq));  // open: gt, lt
  Comparator #(.Bits(8)) comparator_13 (.a(CMD), .b(8'h1), .eq(comparator_13_eq));  // open: gt, lt
  Comparator #(.Bits(8)) comparator_14 (.a(CMD), .b(8'h1), .eq(comparator_14_eq));  // open: gt, lt
  Comparator #(.Bits(8)) comparator_15 (.a(CMD), .b(8'h1), .eq(comparator_15_eq));  // open: gt, lt
  Comparator #(.Bits(8)) comparator_16 (.a(CMD), .b(8'h1), .eq(comparator_16_eq));  // open: gt, lt
  Comparator #(.Bits(8)) comparator_17 (.a(CMD), .b(8'h1), .eq(comparator_17_eq));  // open: gt, lt
  Comparator #(.Bits(8)) comparator_18 (.a(CMD), .b(8'h1), .eq(comparator_18_eq));  // open: gt, lt
  Comparator #(.Bits(8)) comparator_19 (.a(CMD), .b(8'h1), .eq(comparator_19_eq));  // open: gt, lt
  Comparator #(.Bits(8)) comparator_20 (.a(CMD), .b(8'h1), .eq(comparator_20_eq));  // open: gt, lt
  // Flag_Register flag_register_1: pin names not known; wires that end beside it: DAT, flag_register_1_p2, flag_register_1_p3, flag_register_1_p4, flag_register_1_p5, comparator_7_eq, comparator_8_eq, comparator_9_eq, comparator_10_eq, CLK, Q, flag_register_1_p12
  // Adder_Subtractor adder_subtractor_1: pin names not known; wires that end beside it: flag_register_1_p12, register_1_p5, register_2_p5, comparator_11_eq, comparator_12_eq, comparator_13_eq, CLK, Q, flag_register_1_p2, flag_register_1_p3, flag_register_1_p4, flag_register_1_p5
  // Incrementor incrementor_1: pin names not known; wires that end beside it: register_2_p5, comparator_14_eq, comparator_15_eq, CLK, Q, flag_register_1_p2, flag_register_1_p3, flag_register_1_p4, flag_register_1_p5, incrementor_1_p10
  // Comparator comparator_21: pin names not known; wires that end beside it: register_1_p5, register_2_p5, comparator_16_eq, comparator_17_eq, comparator_18_eq, CLK, Q
  // Barrel_Shift_Register barrel_shift_register_1: pin names not known; wires that end beside it: DAT, CLK, register_1_p5, DAT, comparator_19_eq, comparator_20_eq, CLK, Q, Q
  Comparator #(.Bits(8)) comparator_22 (.a(CMD), .b(8'h1), .eq(comparator_22_eq));  // open: gt, lt
  Comparator #(.Bits(8)) comparator_23 (.a(CMD), .b(8'h1), .eq(comparator_23_eq));  // open: gt, lt
  Comparator #(.Bits(8)) comparator_24 (.a(CMD), .b(8'h1), .eq(comparator_24_eq));  // open: gt, lt
  Comparator #(.Bits(8)) comparator_25 (.a(CMD), .b(8'h1), .eq(comparator_25_eq));  // open: gt, lt
  Comparator #(.Bits(8)) comparator_26 (.a(CMD), .b(8'h1), .eq(comparator_26_eq));  // open: gt, lt
  Comparator #(.Bits(8)) comparator_27 (.a(CMD), .b(8'h1), .eq(comparator_27_eq));  // open: gt, lt
  Comparator #(.Bits(8)) comparator_28 (.a(CMD), .b(8'h1), .eq(comparator_28_eq));  // open: gt, lt
  Comparator #(.Bits(8)) comparator_29 (.a(CMD), .b(8'h1), .eq(comparator_29_eq));  // open: gt, lt
  // _8_Input_Or _8_input_or_1: pin names not known; wires that end beside it: register_1_p5, _8_input_or_1_p2
  // _8_Input_Or _8_input_or_2: pin names not known; wires that end beside it: register_2_p5, _8_input_or_2_p2
  // Bitwise_NOT bitwise_not_1: pin names not known; wires that end beside it: register_1_p5, comparator_22_eq, CLK, Q
  // Bitwise_OR bitwise_or_1: pin names not known; wires that end beside it: register_1_p5, register_2_p5, comparator_23_eq, CLK, Q
  // Bitwise_AND bitwise_and_1: pin names not known; wires that end beside it: register_1_p5, register_2_p5, comparator_24_eq, CLK, Q
  // Bitwise_XOR bitwise_xor_1: pin names not known; wires that end beside it: register_1_p5, register_2_p5, comparator_25_eq, CLK, Q
  // Binary_NOT binary_not_1: pin names not known; wires that end beside it: _8_input_or_1_p2, comparator_26_eq, CLK, Q
  // Binary_OR binary_or_1: pin names not known; wires that end beside it: _8_input_or_1_p2, _8_input_or_2_p2, comparator_27_eq, CLK, Q
  // Binary_AND binary_and_1: pin names not known; wires that end beside it: _8_input_or_1_p2, _8_input_or_2_p2, comparator_28_eq, CLK, Q
  // Binary_XOR binary_xor_1: pin names not known; wires that end beside it: CLK, _8_input_or_1_p2, _8_input_or_2_p2, comparator_29_eq, CLK, Q, Q

  // Notes on the sheet:
  //   CMD
  //   DAT
  //   CLK
  //   A
  //   B
  //   C
  //   Q
endmodule
